# Fritzing sketch octave keyboard (saved by Fritzing 1.0.2b)
breadboards: 3

parts:
  S1 = Momentary Switch [package=ksa_sealed_tac_switch]
  S2 = Momentary Switch [package=ksa_sealed_tac_switch]
  S3 = Momentary Switch [package=ksa_sealed_tac_switch]
  S4 = Momentary Switch [package=ksa_sealed_tac_switch]
  S5 = Momentary Switch [package=ksa_sealed_tac_switch]
  S6 = Momentary Switch [package=ksa_sealed_tac_switch]
  S7 = Momentary Switch [package=ksa_sealed_tac_switch]
  S8 = Momentary Switch [package=ksa_sealed_tac_switch]
  S9 = Momentary Switch [package=ksa_sealed_tac_switch]
  S10 = Momentary Switch [package=ksa_sealed_tac_switch]
  S11 = Momentary Switch [package=ksa_sealed_tac_switch]
  S12 = Momentary Switch [package=ksa_sealed_tac_switch]
  S13 = Momentary Switch [package=ksa_sealed_tac_switch]
  R1 = Resistor [tolerance=±5% power=0.25W resistance=220 package=THT]
  R2 = Resistor [tolerance=±5% power=0.25W resistance=220 package=THT]
  R3 = Resistor [tolerance=±5% power=0.25W resistance=220 package=THT]
  R5 = Resistor [tolerance=±5% power=0.25W resistance=220 package=THT]
  R6 = Resistor [tolerance=±5% power=0.25W resistance=220 package=THT]
  R4 = Resistor [tolerance=±5% power=0.25W resistance=220 package=THT]
  R9 = Resistor [tolerance=±5% power=0.25W resistance=220 package=THT]
  R8 = Resistor [tolerance=±5% power=0.25W resistance=220 package=THT]
  R7 = Resistor [tolerance=±5% power=0.25W resistance=220 package=THT]
  R12 = Resistor [tolerance=±5% power=0.25W resistance=220 package=THT]
  R10 = Resistor [tolerance=±5% power=0.25W resistance=220 package=THT]
  R11 = Resistor [tolerance=±5% power=0.25W resistance=220 package=THT]
  Part1 = Adafruit ItsyBitsy M4 [part_number="Adafruit #3800"]
  R0 = Resistor [tolerance=±5% power=0.25W resistance=220 package=THT]
  POT1 = Breadboard Trimpot
  POT2 = Breadboard Trimpot
  R14 = Resistor [tolerance=±5% power=0.25W resistance=33k package=THT]
  POT3 = Breadboard Trimpot
  POT4 = Breadboard Trimpot
  S14 = Momentary Switch [package=ksa_sealed_tac_switch]
  LED1 = LED - 3mm [color="Yellow (592nm)" current=0.030A package="3 mm [THT]"]
  POT5 = Breadboard Trimpot
  U1 = 74HC595 [package="DIP16 [THT]"]
  LED2 = LED - 3mm [color="White (6500K)" current=0.030A package="3 mm [THT]"]
  S15 = Momentary Switch [package=ksa_sealed_tac_switch]
  S16 = Momentary Switch [package=ksa_sealed_tac_switch]
  LED3 = LED - 3mm [color="Red (635nm)" current=0.030A package="3 mm [THT]"]
  LED4 = LED - 3mm [color="Red (635nm)" current=0.030A package="3 mm [THT]"]
  LED5 = LED - 3mm [color="Red (635nm)" current=0.030A package="3 mm [THT]"]
  LED6 = LED - 3mm [color="Red (635nm)" current=0.030A package="3 mm [THT]"]
  LED7 = LED - 3mm [color="Red (635nm)" current=0.030A package="3 mm [THT]"]
  LED8 = LED - 3mm [color="Red (635nm)" current=0.030A package="3 mm [THT]"]
  LED9 = LED - 3mm [color="White (6500K)" current=0.030A package="3 mm [THT]"]
  R15 = Resistor [tolerance=±5% power=0.25W resistance=33k package=THT]
  R16 = Resistor [tolerance=±5% power=0.25W resistance=33k package=THT]
  R17 = Resistor [tolerance=±5% power=0.25W resistance=470 package=THT]
  R18 = Resistor [tolerance=±5% power=0.25W resistance=470 package=THT]
  R20 = Resistor [tolerance=±5% power=0.25W resistance=470 package=THT]
  R21 = Resistor [tolerance=±5% power=0.25W resistance=470 package=THT]
  R22 = Resistor [tolerance=±5% power=0.25W resistance=470 package=THT]
  R24 = Resistor [tolerance=±5% power=0.25W resistance=470 package=THT]
  R25 = Resistor [tolerance=±5% power=0.25W resistance=470 package=THT]
  R26 = Resistor [tolerance=±5% power=0.25W resistance=33k package=THT]
  R27 = Resistor [tolerance=±5% power=0.25W resistance=470 package=THT]
  R23 = Resistor [tolerance=±5% power=0.25W resistance=470 package=THT]
  R28 = Resistor [tolerance=±5% power=0.25W resistance=470 package=THT]
  LED10 = LED - 3mm [color="Blue (430nm)" current=0.030A package="3 mm [THT]"]
  POT6 = Breadboard Trimpot
  S17 = Momentary Switch [package=ksa_sealed_tac_switch]
  S18 = Momentary Switch [package=ksa_sealed_tac_switch]
  R29 = Resistor [tolerance=±5% power=0.25W resistance=33k package=THT]
  R30 = Resistor [tolerance=±5% power=0.25W resistance=33k package=THT]
  LED11 = LED - 3mm [color="Green (555nm)" current=0.030A package="3 mm [THT]"]
  R31 = Resistor [tolerance=±5% power=0.25W resistance=470 package=THT]

nets:
  N1: S1.2, S2.2, S3.2, S4.2, S5.2, Part1.A2, R14.Pin_0
  N2: S1.3, R1.Pin_0, R0.Pin_1
  N3: S2.3, R1.Pin_1, R2.Pin_0
  N4: S3.3, R2.Pin_1, R3.Pin_0
  N5: S4.3, R3.Pin_1, R4.Pin_0
  N6: S5.3, R5.Pin_0, R4.Pin_1
  N7: S6.3, R5.Pin_1, R6.Pin_0
  N8: S7.3, R6.Pin_1, R7.Pin_0
  N9: S8.3, R8.Pin_0, R7.Pin_1
  N10: S9.2, S10.2, S11.2, S12.2, S13.2
  N11: S9.3, R9.Pin_0, R8.Pin_1
  N12: S10.3, R9.Pin_1, R10.Pin_0
  N13: S11.3, R10.Pin_1, R11.Pin_0
  N14: S12.3, R12.Pin_0, R11.Pin_1
  +3V3: S13.3, R12.Pin_1, Part1.+3V3, POT1.PIN3, POT2.PIN3, POT3.PIN3, POT4.PIN3, POT5.PIN3, U1.MR, U1.VCC, R15.Pin_1, R16.Pin_1, R26.Pin_1, POT6.PIN3, R29.Pin_1, R30.Pin_1
  GND: Part1.GND, R0.Pin_0, POT1.PIN1, POT2.PIN1, R14.Pin_1, POT3.PIN1, POT4.PIN1, S14.1, LED1.cathode, POT5.PIN1, U1.GND, U1.OE, LED2.cathode, S15.1, S15.2, S16.1, S16.2, LED3.cathode, LED4.cathode, LED5.cathode, LED6.cathode, LED7.cathode, LED8.cathode, LED9.cathode, LED10.anode, POT6.PIN1, S17.1, S17.2, S18.1, S18.2, LED11.anode
  N15: Part1.D13, R27.Pin_0
  N16: Part1.D10, S14.3, R26.Pin_0
  N17: Part1.D9, S16.3, S16.4, R16.Pin_0
  N18: Part1.D7, S15.3, S15.4, R15.Pin_0
  N19: Part1.D5_5V, U1.ST_CP
  N20: Part1.SCL, R30.Pin_0
  N21: Part1.SDA, S17.3, S17.4, R29.Pin_0
  N22: Part1.TX_D1, POT6.PIN2
  N23: Part1.RX_D0, R31.Pin_0
  N24: Part1.MOSI, U1.DS
  N25: Part1.SCK, U1.SH_CP
  N26: Part1.A5, POT4.PIN2
  N27: Part1.A4, POT3.PIN2
  N28: Part1.A3, POT5.PIN2
  N29: Part1.A1, POT2.PIN2
  N30: Part1.A0, POT1.PIN2
  N31: LED1.anode, R27.Pin_1
  N32: U1.Q1, R17.Pin_0
  N33: U1.Q2, R18.Pin_0
  N34: U1.Q3, R24.Pin_0
  N35: U1.Q4, R20.Pin_0
  N36: U1.Q5, R21.Pin_0
  N37: U1.Q6, R22.Pin_0
  N38: U1.Q7, R23.Pin_0
  N39: U1.Q0, R25.Pin_0
  N40: LED2.anode, R25.Pin_1
  N41: LED3.anode, R17.Pin_1
  N42: LED4.anode, R18.Pin_1
  N43: LED5.anode, R24.Pin_1
  N44: LED6.anode, R23.Pin_1
  N45: LED7.anode, R22.Pin_1
  N46: LED8.anode, R21.Pin_1
  N47: LED9.anode, R20.Pin_1
  N48: R28.Pin_1, LED10.cathode
  N49: S18.3, S18.4
  N50: LED11.cathode, R31.Pin_1

notes:
  PWM 1 AND 2 OUTPUT
  <-- PITCH DETUNE -->
  <-- PWM1 PWM2 On/Off PWM2 -->
  REC SKIP TEMPO
  RAND THRESHOLD
  ARP REC ARP ON

custom parts:
  Adafruit ItsyBitsy M4: What's smaller than a Feather but larger than a Trinket? It's an Adafruit ItsyBitsy M4 Express featuring the Microchip ATSAMD51! Small, powerful, with a ultra fast ATSAMD51 Cortex M4 processor running at 120 MHz - this microcontroller board is perfect when you want something very compact, with a ton of horsepower and a bunch of pins. This Itsy is like a bullet train, with it's 120MHz Cortex M4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

// code stored in the sketch: PWM Synth.bas

